// Logisim project Compteur.circ as structural Verilog: 1 circuit, main circuit main
module main (
  output [7:0] outCompteur
);

  wire clock_1_out, d_ff_1_q, d_ff_2_q, d_ff_3_q, d_ff_4_q, d_ff_5_q, d_ff_6_q, d_ff_7_q, d_ff_8_q;

  Clock clock_1 (.out(clock_1_out));
  D_Flip_Flop d_ff_1 (
    .clk(clock_1_out), .D(outCompteur[0]), .Q(d_ff_1_q), .Qn(outCompteur[0]));  // open: preset, en, reset
  D_Flip_Flop d_ff_2 (
    .clk(d_ff_1_q), .D(outCompteur[1]), .Q(d_ff_2_q), .Qn(outCompteur[1]));  // open: preset, en, reset
  D_Flip_Flop d_ff_3 (
    .clk(d_ff_2_q), .D(outCompteur[2]), .Q(d_ff_3_q), .Qn(outCompteur[2]));  // open: preset, en, reset
  D_Flip_Flop d_ff_4 (
    .clk(d_ff_3_q), .D(outCompteur[3]), .Q(d_ff_4_q), .Qn(outCompteur[3]));  // open: preset, en, reset
  D_Flip_Flop d_ff_5 (
    .clk(d_ff_4_q), .D(outCompteur[4]), .Q(d_ff_5_q), .Qn(outCompteur[4]));  // open: preset, en, reset
  D_Flip_Flop d_ff_6 (
    .clk(d_ff_5_q), .D(outCompteur[5]), .Q(d_ff_6_q), .Qn(outCompteur[5]));  // open: preset, en, reset
  D_Flip_Flop d_ff_7 (
    .clk(d_ff_6_q), .D(outCompteur[6]), .Q(d_ff_7_q), .Qn(outCompteur[6]));  // open: preset, en, reset
  D_Flip_Flop d_ff_8 (
    .clk(d_ff_7_q), .D(outCompteur[7]), .Q(d_ff_8_q), .Qn(outCompteur[7]));  // open: preset, en, reset

  // Other names for the same wires on the sheet: q7 = outCompteur[0]; q6 = outCompteur[1]; q5 = outCompteur[2];
  //   q4 = outCompteur[3]; q3 = outCompteur[4]; q2 = outCompteur[5]; q1 = outCompteur[6]; q0 = outCompteur[7]
endmodule
