// Logisim project Controller.circ as structural Verilog: 7 circuits, main circuit compteur
module compteur (
  input  clocksys,
  output [7:0] outCompteur
);

  wire d_ff_1_q, d_ff_2_q, d_ff_3_q, d_ff_4_q, d_ff_5_q, d_ff_6_q, d_ff_7_q, d_ff_8_q;

  D_Flip_Flop d_ff_1 (
    .clk(clocksys), .D(outCompteur[0]), .Q(d_ff_1_q), .Qn(outCompteur[0]));  // open: preset, en, reset
  D_Flip_Flop d_ff_2 (
    .clk(d_ff_1_q), .D(outCompteur[1]), .Q(d_ff_2_q), .Qn(outCompteur[1]));  // open: preset, en, reset
  D_Flip_Flop d_ff_3 (
    .clk(d_ff_2_q), .D(outCompteur[2]), .Q(d_ff_3_q), .Qn(outCompteur[2]));  // open: preset, en, reset
  D_Flip_Flop d_ff_4 (
    .clk(d_ff_3_q), .D(outCompteur[3]), .Q(d_ff_4_q), .Qn(outCompteur[3]));  // open: preset, en, reset
  D_Flip_Flop d_ff_5 (
    .clk(d_ff_4_q), .D(outCompteur[4]), .Q(d_ff_5_q), .Qn(outCompteur[4]));  // open: preset, en, reset
  D_Flip_Flop d_ff_6 (
    .clk(d_ff_5_q), .D(outCompteur[5]), .Q(d_ff_6_q), .Qn(outCompteur[5]));  // open: preset, en, reset
  D_Flip_Flop d_ff_7 (
    .clk(d_ff_6_q), .D(outCompteur[6]), .Q(d_ff_7_q), .Qn(outCompteur[6]));  // open: preset, en, reset
  D_Flip_Flop d_ff_8 (
    .clk(d_ff_7_q), .D(outCompteur[7]), .Q(d_ff_8_q), .Qn(outCompteur[7]));  // open: preset, en, reset

  // Other names for the same wires on the sheet: q7 = outCompteur[0]; q6 = outCompteur[1]; q5 = outCompteur[2];
  //   q4 = outCompteur[3]; q3 = outCompteur[4]; q2 = outCompteur[5]; q1 = outCompteur[6]; q0 = outCompteur[7]
endmodule

// Inst
module controleur (
  input  Reset,
  output clk,
  output [7:0] PC,
  output ldRam,
  output selRam,
  output [4:0] Imm5,
  output [2:0] Rn,
  output [7:0] Imm8,
  output Load___Store,
  output [3:0] Codop,
  output [2:0] Rm,
  output [2:0] Rd
);

  wire instructiondecodeur_1_branch, instructiondecodeur_1_data_processing, instructiondecodeur_1_load_store,
       instructiondecodeur_1_shit, ldC, lsA, lsB, lsC, lsD, selRamC;
  wire [1:0] selType;
  wire [2:0] rdA, rdB, rdC, rdD, rmA, rmB, rmC, rmD, rnA, rnB, rnC, rnD;
  wire [3:0] codopA, codopB, codopC, codopD;
  wire [4:0] Imm5A, Imm5B, Imm5C, Imm5D;
  wire [7:0] Imm8A, Imm8B, Imm8C, Imm8D;
  wire [15:0] main_1_inst;

  Clock clock (.out(clk));
  ROM_main main_1 (.Address(PC), .Inst(main_1_inst));  // open: Sel
  // Probe on main_1_inst
  compteur Compteur (.clocksys(clk), .outCompteur(PC));
  instructionDecodeur instructiondecodeur_1 (
    .Inst(main_1_inst), .shit(instructiondecodeur_1_shit),
    .data_processing(instructiondecodeur_1_data_processing), .load_store(instructiondecodeur_1_load_store),
    .branch(instructiondecodeur_1_branch));
  Multiplexer #(.select(2)) multiplexer_1 (
    .in0(lsA), .in1(lsB), .in2(lsC), .in3(lsD), .out(Load___Store), .sel(selType), .en(1'b1));
  _4bTo2b u_4bto2b_1 (
    .catA(instructiondecodeur_1_shit), .catB(instructiondecodeur_1_data_processing),
    .catC(instructiondecodeur_1_load_store), .catD(instructiondecodeur_1_branch), .selCat(selType));
  categoryAbis categoryabis_1 (
    .in_1(main_1_inst), .Load___Store(lsA), .Codop(codopA), .rm(rmA), .Rd(rdA), .rn(rnA), .Imm8(Imm8A),
    .Imm5(Imm5A));
  dataProcessing_main main_2 (.in_1(main_1_inst), .opcode(codopB), .rd(rdB), .rn(rnB), .rm(rmB));
  loadstoreSortie loadstoresortie_1 (.inst(main_1_inst), .Imm8(Imm8C), .rd(rdC), .ldRam(ldC), .selRAM(selRamC));
  Multiplexer #(.select(2), .width(4)) multiplexer_2 (
    .in0(codopA), .in1(codopB), .in2(codopC), .in3(codopD), .out(Codop), .sel(selType), .en(1'b1));
  Multiplexer #(.select(2)) multiplexer_3 (
    .in2(selRamC), .out(selRam), .sel(selType), .en(1'b1));  // open: in0, in1, in3
  Multiplexer #(.select(2), .width(3)) multiplexer_4 (
    .in0(rnA), .in1(rnB), .in2(rnC), .in3(rnD), .out(Rn), .sel(selType), .en(1'b1));
  Multiplexer #(.select(2)) multiplexer_5 (.in2(ldC), .out(ldRam), .sel(selType), .en(1'b1));  // open: in0, in1, in3
  Multiplexer #(.select(2), .width(5)) multiplexer_6 (
    .in0(Imm5A), .in1(Imm5B), .in2(Imm5C), .in3(Imm5D), .out(Imm5), .sel(selType), .en(1'b1));
  Multiplexer #(.select(2), .width(3)) multiplexer_7 (
    .in0(rmA), .in1(rmB), .in2(rmC), .in3(rmD), .out(Rm), .sel(selType), .en(1'b1));
  Multiplexer #(.select(2), .width(8)) multiplexer_8 (
    .in0(Imm8A), .in1(Imm8B), .in2(Imm8C), .in3(Imm8D), .out(Imm8), .sel(selType), .en(1'b1));
  Multiplexer #(.select(2), .width(3)) multiplexer_9 (
    .in0(rdA), .in1(rdB), .in2(rdC), .in3(rdD), .out(Rd), .sel(selType), .en(1'b1));

  // Other names for the same wires on the sheet: clock = clk
endmodule

module instructionDecodeur (
  input  [15:0] Inst,
  output shit,
  output data_processing,
  output load_store,
  output branch
);

  selecteurCategory selecteurCategory (
    .i0(Inst[10]), .i1(Inst[11]), .i2(Inst[12]), .i3(Inst[13]), .i4(Inst[14]), .i5(Inst[15]), .out0(shit),
    .out1(data_processing), .out2(load_store), .out3(branch));
endmodule

module selecteurCategory (
  input  i0,
  input  i1,
  input  i2,
  input  i3,
  input  i4,
  input  i5,
  output out0,
  output out1,
  output out2,
  output out3
);

  wire and_1_out, not_1_out, not_2_out, not_3_out, not_4_out, not_5_out, not_6_out, not_7_out, not_8_out,
       not_9_out, not_10_out, not_11_out;

  not not_1 (not_1_out, i3);
  not not_2 (not_2_out, i5);
  not not_3 (not_3_out, i4);
  not not_4 (not_4_out, i5);
  not not_5 (not_5_out, i3);
  not not_6 (not_6_out, i2);
  not not_7 (not_7_out, i1);
  not not_8 (not_8_out, i0);
  not not_9 (not_9_out, i3);
  and and_1 (and_1_out, not_2_out, not_3_out);
  and and_2 (out1, not_4_out, i4, not_5_out, not_6_out, not_7_out, not_8_out);
  not not_10 (not_10_out, i4);
  and and_3 (out3, i5, i4, not_9_out, i2);
  not not_11 (not_11_out, out2);
  and and_4 (out0, not_11_out, and_1_out);
  and and_5 (out2, i5, not_10_out, not_1_out, i2);

  // Notes on the sheet:
  //   DATA PROCESSING
  //   LOAD STORE
  //   BRANCH
  //   SHIT ADD SUB MOVE
endmodule

module loadstoreSortie (
  input  [15:0] inst,
  output [7:0] Imm8,
  output [2:0] rd,
  output ldRam,
  output selRAM
);

  BitSelector #(.width(16)) bitselector_1 (.in(inst), .out(ldRam), .sel(4'b1011));

  assign Imm8 = inst[7:0];
  assign rd = inst[10:8];
  assign selRAM = 1'b1;
endmodule

module DataProcessing (
  input  [15:0] inst,
  output [3:0] CODOP,
  output [2:0] Rm,
  output [2:0] Rdn
);

  instructionDecodeur instructiondecodeur_1 ();  // open: Inst, shit, data_processing, load_store, branch
  // Probe on inst[5:0]

  assign CODOP = inst[9:6];
  assign Rdn = inst[15:13];
  assign Rm = inst[12:10];
endmodule

module _4bTo2b (
  input  catA,
  input  catB,
  input  catC,
  input  catD,
  output [1:0] selCat
);

  wire not_1_out, not_2_out, not_3_out, not_4_out;

  not not_1 (not_1_out, catC);
  not not_2 (not_2_out, catD);
  not not_3 (not_3_out, catB);
  not not_4 (not_4_out, catD);
  and and_1 (selCat[0], not_1_out, not_2_out);
  and and_2 (selCat[1], not_3_out, not_4_out);
endmodule
