// Logisim project ProjetPEP.circ as structural Verilog: 4 circuits, main circuit main
module main (
  input  [31:0] in_1
);

  wire CarryIn, clk, Clr, Id, ld, Load_Store, Reset, Sel;
  wire [2:0] RegA, RegB, RegDest;
  wire [3:0] Codop, Flags;
  wire [4:0] Shifter;
  wire [7:0] Adress;
  wire [31:0] alu_1_s, multiplexer_1_out, ramm_1_dataout, register_1_aout, register_1_bout;

  controleur controleur_1 (
    .clk(clk), .ldRam(Id), .selRam(Sel), .Imm5(Shifter), .Rn(RegB), .Imm8(Adress), .Load___Store(Load_Store),
    .Codop(Codop), .Rm(RegA), .Rd(RegDest));  // open: Reset, PC
  // Probe on register_1_bout
  // Probe on alu_1_s
  // Probe on Adress
  Multiplexer #(.width(32), .enable("false")) multiplexer_1 (
    .in0(alu_1_s), .in1(ramm_1_dataout), .out(multiplexer_1_out), .sel(ld));
  Register register_1 (
    .RegA(RegA), .DataIn(multiplexer_1_out), .RegB(RegB), .RegDest(RegDest), .clk(clk), .Reset(Reset),
    .Aout(register_1_aout), .Bout(register_1_bout));
  RAMM ramm_1 (.Clr(Clr), .sel(Sel), .ld(Id), .clk(clk), .Address(Adress), .DataIn(in_1), .DataOut(ramm_1_dataout));
  // Probe on RegDest
  ALU alu_1 (
    .A(register_1_aout), .B(register_1_bout), .Shifter(Shifter), .CarryIn(CarryIn), .Codop(Codop),
    .Flags(Flags), .S(alu_1_s));
  // Probe on register_1_aout
  // Probe on multiplexer_1_out

  // Other names for the same wires on the sheet: DataIn[31:0] = in_1

  // Notes on the sheet:
  //   RAM
  //   Banc de Registres
  //   ALU
endmodule

module ALU (
  input  [31:0] A,
  input  [31:0] B,
  input  [4:0] Shifter,
  input  CarryIn,
  input  [3:0] Codop,
  output [3:0] Flags,
  output [31:0] S
);

  wire bitselector_1_out, bitselector_2_out, bitselector_3_out, bitselector_4_out, bitselector_5_out,
       bitselector_6_out, bitselector_7_out, bitselector_8_out, bitselector_9_out, bitselector_10_out,
       bitselector_11_out, bitselector_12_out, CarryOut_A_B, CarryOut_A_B_Cin, CarryOut_A_B_Cin_t,
       CarryOut_A_B_t, comparator_1_eq, comparator_3_eq, comparator_4_eq, comparator_5_eq, comparator_6_eq,
       comparator_7_eq, comparator_8_eq, comparator_9_eq, not_2_out, not_4_out, not_5_out, not_6_out,
       Overflow_A_B, Overflow_A_B_Cin, Overflow_A_B_Cin_t, Overflow_A_B_t;
  wire [31:0] _0_B, A_and_B, A_and_not_B, A_B, A_B_Cin, A_B_Cin_t, A_B_t, A_B_t_t, A_or_B, A_xor_B,
       B____shift, B____shift__arith, B____shift__rot, B____shift_t, not_1_out, NOT_B, not_B_t;

  Multiplexer #(.select(4), .enable("false")) multiplexer_1 (
    .in0(1'b0), .in1(1'b0), .in2(1'b0), .in3(1'b0), .in4(1'b0), .in5(CarryOut_A_B_Cin),
    .in6(CarryOut_A_B_Cin_t), .in7(1'b0), .in8(1'b0), .in9(1'b0), .in10(CarryOut_A_B_t), .in11(CarryOut_A_B),
    .in12(1'b0), .in13(1'b0), .in14(1'b0), .in15(1'b0), .out(Flags[1]), .sel(Codop));
  Multiplier #(.width(32)) multiplier_1 (.a(A), .b(B), .out(A_B));  // open: cin, cout
  assign not_1_out = ~B;  // NOT_Gate not_1, 32 bits wide
  assign A_xor_B = A ^ B;  // XOR_Gate xor_1, 32 bits wide
  assign A_or_B = A | B;  // OR_Gate or_1, 32 bits wide
  Shifter #(.width(32), .shift("lr")) shifter_1 (.in(B), .\dist (Shifter), .out(B____shift_t));
  Subtractor #(.width(32)) subtractor_1 (.a(A), .b(B), .out(A_B_t_t), .bout(CarryOut_A_B_t));  // open: bin
  BitSelector #(.width(32)) bitselector_1 (.in(A), .out(bitselector_1_out), .sel({5{1'b1}}));
  BitSelector #(.width(32)) bitselector_2 (.in(B), .out(bitselector_2_out), .sel({5{1'b1}}));
  assign A_and_not_B = A & not_1_out;  // AND_Gate and_1, 32 bits wide
  Multiplexer #(.select(4), .width(32), .enable("false")) multiplexer_2 (
    .in0(A_and_B), .in1(A_xor_B), .in2(B____shift), .in3(B____shift_t), .in4(B____shift__arith),
    .in5(A_B_Cin), .in6(A_B_Cin_t), .in7(B____shift__rot), .in8(A_and_B), .in9(_0_B), .in10(A_B_t_t),
    .in11(A_B_t), .in12(A_or_B), .in13(A_B), .in14(A_and_not_B), .in15(not_B_t), .out(S), .sel(Codop));
  BitSelector #(.width(32)) bitselector_3 (.in(A_B_t_t), .out(bitselector_3_out), .sel({5{1'b1}}));
  Comparator #(.width(1)) comparator_1 (
    .a(bitselector_1_out), .b(bitselector_2_out), .eq(comparator_1_eq));  // open: gt, lt
  Comparator #(.width(32)) comparator_2 (.a(S), .b({32{1'b0}}), .eq(Flags[3]), .lt(Flags[2]));  // open: gt
  not not_2 (not_2_out, comparator_3_eq);
  Comparator #(.width(1)) comparator_3 (
    .a(bitselector_3_out), .b(bitselector_1_out), .eq(comparator_3_eq));  // open: gt, lt
  and and_2 (Overflow_A_B_t, not_2_out, comparator_1_eq);
  Multiplexer #(.select(4), .enable("false")) multiplexer_3 (
    .in0(1'b0), .in1(1'b0), .in2(1'b0), .in3(1'b0), .in4(1'b0), .in5(Overflow_A_B_Cin),
    .in6(Overflow_A_B_Cin_t), .in7(1'b0), .in8(1'b0), .in9(1'b0), .in10(Overflow_A_B_t), .in11(Overflow_A_B),
    .in12(1'b0), .in13(1'b0), .in14(1'b0), .in15(1'b0), .out(Flags[0]), .sel(Codop));
  Subtractor #(.width(32)) subtractor_2 (.a({32{1'b0}}), .b(B), .out(_0_B));  // open: bin, bout
  assign NOT_B = ~B;  // NOT_Gate not_3, 32 bits wide
  Shifter #(.width(32), .shift("ar")) shifter_2 (.in(B), .\dist (Shifter), .out(B____shift__arith));
  assign A_and_B = A & B;  // AND_Gate and_3, 32 bits wide
  Shifter #(.width(32)) shifter_3 (.in(B), .\dist (Shifter), .out(B____shift));
  Adder #(.width(32)) adder_1 (.a(A), .b(B), .out(A_B_t_t), .cout(CarryOut_A_B));  // open: cin
  BitSelector #(.width(32)) bitselector_4 (.in(A), .out(bitselector_4_out), .sel({5{1'b1}}));
  BitSelector #(.width(32)) bitselector_5 (.in(B), .out(bitselector_5_out), .sel({5{1'b1}}));
  BitSelector #(.width(32)) bitselector_6 (.in(A_B_t_t), .out(bitselector_6_out), .sel({5{1'b1}}));
  Adder #(.width(32)) adder_2 (.a(A), .b(B), .out(A_B_t_t), .cin(CarryIn), .cout(CarryOut_A_B_Cin));
  Subtractor #(.width(32)) subtractor_3 (.a(A), .b(B), .out(A_B_t_t), .bin(CarryIn), .bout(CarryOut_A_B_Cin_t));
  Comparator #(.width(1)) comparator_4 (
    .a(bitselector_4_out), .b(bitselector_5_out), .eq(comparator_4_eq));  // open: gt, lt
  BitSelector #(.width(32)) bitselector_7 (.in(A_B_t_t), .out(bitselector_7_out), .sel({5{1'b1}}));
  BitSelector #(.width(32)) bitselector_8 (.in(A), .out(bitselector_8_out), .sel({5{1'b1}}));
  BitSelector #(.width(32)) bitselector_9 (.in(B), .out(bitselector_9_out), .sel({5{1'b1}}));
  BitSelector #(.width(32)) bitselector_10 (.in(A_B_t_t), .out(bitselector_10_out), .sel({5{1'b1}}));
  BitSelector #(.width(32)) bitselector_11 (.in(A), .out(bitselector_11_out), .sel({5{1'b1}}));
  BitSelector #(.width(32)) bitselector_12 (.in(B), .out(bitselector_12_out), .sel({5{1'b1}}));
  Comparator #(.width(1)) comparator_5 (
    .a(bitselector_6_out), .b(bitselector_4_out), .eq(comparator_5_eq));  // open: gt, lt
  Shifter #(.width(32), .shift("rr")) shifter_4 (.in(B), .\dist (Shifter), .out(B____shift__rot));
  not not_4 (not_4_out, comparator_5_eq);
  and and_4 (Overflow_A_B, not_4_out, comparator_4_eq);
  Comparator #(.width(1)) comparator_6 (
    .a(bitselector_7_out), .b(bitselector_8_out), .eq(comparator_6_eq));  // open: gt, lt
  Comparator #(.width(1)) comparator_7 (
    .a(bitselector_8_out), .b(bitselector_9_out), .eq(comparator_7_eq));  // open: gt, lt
  Comparator #(.width(1)) comparator_8 (
    .a(bitselector_10_out), .b(bitselector_11_out), .eq(comparator_8_eq));  // open: gt, lt
  Comparator #(.width(1)) comparator_9 (
    .a(bitselector_11_out), .b(bitselector_12_out), .eq(comparator_9_eq));  // open: gt, lt
  not not_5 (not_5_out, comparator_6_eq);
  and and_5 (Overflow_A_B_Cin, not_5_out, comparator_7_eq);
  not not_6 (not_6_out, comparator_8_eq);
  and and_6 (Overflow_A_B_Cin_t, not_6_out, comparator_9_eq);

  // Other names for the same wires on the sheet: Overflow = Flags[0]; CarryOut = Flags[1]; Negatif = Flags[2];
  //   Zero = Flags[3]

  // Notes on the sheet:
  //   A XNOR B
  //   A OR B
  //   B >> shift
  //   A*B
  //   A AND not B
  //   A-B
  //   B >> shift (arith)
  //   0-B
  //   B << shift
  //   A AND B
  //   not B
  //   A+B
  //   B >> shift (rot)
  //   A+B+Cin
  //   A-B+Cin
endmodule

module Register (
  input  [2:0] RegA,
  input  [31:0] DataIn,
  input  [2:0] RegB,
  input  clk,
  input  Reset,
  input  [2:0] RegDest,
  output [31:0] Aout,
  output [31:0] Bout
);

  wire decoder_1_out0, decoder_1_out1, decoder_1_out2, decoder_1_out3, decoder_1_out4, decoder_1_out5,
       decoder_1_out6, decoder_1_out7;
  wire [31:0] register_1_q, register_2_q, register_3_q, register_4_q, register_5_q, register_6_q,
       register_7_q, register_8_q;

  Decoder #(.select(3), .enable("false")) decoder_1 (
    .out0(decoder_1_out0), .out1(decoder_1_out1), .out2(decoder_1_out2), .out3(decoder_1_out3),
    .out4(decoder_1_out4), .out5(decoder_1_out5), .out6(decoder_1_out6), .out7(decoder_1_out7), .sel(RegDest));
  Register_part #(.width(32)) register_1 (.D(DataIn), .en(decoder_1_out0), .Q(register_1_q), .clk(clk), .clr(Reset));
  Register_part #(.width(32)) register_2 (.D(DataIn), .en(decoder_1_out1), .Q(register_2_q), .clk(clk), .clr(Reset));
  Register_part #(.width(32)) register_3 (.D(DataIn), .en(decoder_1_out2), .Q(register_3_q), .clk(clk), .clr(Reset));
  Register_part #(.width(32)) register_4 (.D(DataIn), .en(decoder_1_out3), .Q(register_4_q), .clk(clk), .clr(Reset));
  Register_part #(.width(32)) register_5 (.D(DataIn), .en(decoder_1_out4), .Q(register_5_q), .clk(clk), .clr(Reset));
  Register_part #(.width(32)) register_6 (.D(DataIn), .en(decoder_1_out5), .Q(register_6_q), .clk(clk), .clr(Reset));
  Register_part #(.width(32)) register_7 (.D(DataIn), .en(decoder_1_out6), .Q(register_7_q), .clk(clk), .clr(Reset));
  Register_part #(.width(32)) register_8 (.D(DataIn), .en(decoder_1_out7), .Q(register_8_q), .clk(clk), .clr(Reset));
  Multiplexer #(.select(3), .width(32), .enable("false")) multiplexer_1 (
    .in0(register_1_q), .in1(register_2_q), .in2(register_3_q), .in3(register_4_q), .in4(register_5_q),
    .in5(register_6_q), .in6(register_7_q), .in7(register_8_q), .out(Aout), .sel(RegA));
  Multiplexer #(.select(3), .width(32), .enable("false")) multiplexer_2 (
    .in0(register_1_q), .in1(register_2_q), .in2(register_3_q), .in3(register_4_q), .in4(register_5_q),
    .in5(register_6_q), .in6(register_7_q), .in7(register_8_q), .out(Bout), .sel(RegB));
endmodule

module RAMM (
  input  Clr,
  input  sel,
  input  ld,
  input  clk,
  input  [31:0] DataIn,
  input  [7:0] Address,
  output [31:0] DataOut
);

  wire store;

  not not_1 (store, ld);
  RAM #(.bus("separate")) ram_1 (
    .addr(Address), .din(DataIn[7:0]), .data(DataOut[7:0]), .str(store), .sel(sel), .clk(clk), .ld(ld),
    .clr(Clr));
  RAM #(.bus("separate")) ram_2 (
    .addr(Address), .din(DataIn[15:8]), .data(DataOut[15:8]), .str(store), .sel(sel), .clk(clk), .ld(ld),
    .clr(Clr));
  RAM #(.bus("separate")) ram_3 (
    .addr(Address), .din(DataIn[23:16]), .data(DataOut[23:16]), .str(store), .sel(sel), .clk(clk), .ld(ld),
    .clr(Clr));
  RAM #(.bus("separate")) ram_4 (
    .addr(Address), .din(DataIn[31:24]), .data(DataOut[31:24]), .str(store), .sel(sel), .clk(clk), .ld(ld),
    .clr(Clr));

  // Other names for the same wires on the sheet: DataIn0[7:0] = DataIn[7:0]; DataIn1[7:0] = DataIn[15:8];
  //   DataIn2[7:0] = DataIn[23:16]; DataIn3[7:0] = DataIn[31:24]; DataOut0[7:0] = DataOut[7:0];
  //   DataOut1[7:0] = DataOut[15:8]; DataOut2[7:0] = DataOut[23:16]; DataOut3[7:0] = DataOut[31:24]
endmodule
