// Logisim project RAM.circ as structural Verilog: 1 circuit, main circuit main
module main (
  input  Clr,
  input  sel,
  input  ld,
  input  clk,
  input  [31:0] DataIn,
  input  [7:0] Address,
  output [31:0] DataOut
);

  RAM #(.bus("separate")) ram_1 (
    .addr(Address), .din(DataIn[7:0]), .data(DataOut[7:0]), .sel(sel), .clk(clk), .ld(ld), .clr(Clr));  // open: str
  RAM #(.bus("separate")) ram_2 (
    .addr(Address), .din(DataIn[15:8]), .data(DataOut[15:8]), .sel(sel), .clk(clk), .ld(ld), .clr(Clr));  // open: str
  RAM #(.bus("separate")) ram_3 (
    .addr(Address), .din(DataIn[23:16]), .data(DataOut[23:16]), .sel(sel), .clk(clk), .ld(ld), .clr(Clr));  // open: str
  RAM #(.bus("separate")) ram_4 (
    .addr(Address), .din(DataIn[31:24]), .data(DataOut[31:24]), .sel(sel), .clk(clk), .ld(ld), .clr(Clr));  // open: str

  // Other names for the same wires on the sheet: DataIn0[7:0] = DataIn[7:0]; DataIn1[7:0] = DataIn[15:8];
  //   DataIn2[7:0] = DataIn[23:16]; DataIn3[7:0] = DataIn[31:24]; DataOut0[7:0] = DataOut[7:0];
  //   DataOut1[7:0] = DataOut[15:8]; DataOut2[7:0] = DataOut[23:16]; DataOut3[7:0] = DataOut[31:24]
endmodule
