// Logisim project ROM.circ as structural Verilog: 1 circuit, main circuit main
module main (
  input  [7:0] Address,
  input  Sel,
  output [15:0] Inst
);

  ROM #(.dataWidth(16)) rom_1 (.addr(Address), .data(Inst), .sel(Sel));
endmodule
